# Fritzing sketch Schema (saved by Fritzing 0.9.3b)
perfboards: 1

parts:
  J1 = longpad pin header, 16 pins [form="long pad"]
  J2 = longpad pin header, 16 pins [form="long pad"]
  J3 = longpad pin header, 16 pins [form="long pad"]
  J4 = longpad pin header, 16 pins [form="long pad"]
  J5 = longpad pin header, 16 pins [form="long pad"]
  J6 = longpad pin header, 16 pins [form="long pad"]
  J7 = longpad pin header, 16 pins [form="long pad"]
  J8 = longpad pin header, 16 pins [form="long pad"]
  J9 = longpad pin header, 16 pins [form="long pad"]
  J10 = longpad pin header, 16 pins [form="long pad"]
  J11 = longpad pin header, 16 pins [form="long pad"]
  J12 = longpad pin header, 16 pins [form="long pad"]
  J13 = longpad pin header, 16 pins [form="long pad"]
  J14 = longpad pin header, 16 pins [form="long pad"]
  J15 = longpad pin header, 16 pins [form="long pad"]
  J19 = longpad pin header, 16 pins [form="long pad"]
  J20 = longpad pin header, 4 pins [form="long pad"]
  J21 = longpad pin header, 4 pins [form="long pad"]
  J22 = longpad pin header, 4 pins [form="long pad"]
  J23 = longpad pin header, 4 pins [form="long pad"]
  J24 = longpad pin header, 4 pins [form="long pad"]
  J25 = longpad pin header, 4 pins [form="long pad"]
  J26 = longpad pin header, 4 pins [form="long pad"]
  J27 = longpad pin header, 4 pins [form="long pad"]
  J28 = longpad pin header, 10 pins [form="long pad"]
  J29 = longpad pin header, 10 pins [form="long pad"]
  U1 = 74HC595 [package="DIP16 [THT]"]
  U2 = 74HC595 [package="DIP16 [THT]"]
  J31 = longpad pin header, 6 pins [form="long pad"]
  S2 = Pushbutton [package=THT]
  J32 = longpad pin header, 2 pins [form="long pad"]

nets:
  N1: J1.pin6, J2.pin6
  N2: J1.pin9, U1.Q0
  N3: J1.pin10, U2.Q0
  N4: J2.pin9, J2.pin10
  N5: J3.pin6, J4.pin6
  N6: J3.pin9, U1.Q1
  N7: J3.pin10, U2.Q1
  N8: J4.pin9, J4.pin10
  N9: J5.pin6, J6.pin6
  N10: J5.pin9, U1.Q2
  N11: J5.pin10, U2.Q2
  N12: J6.pin9, J6.pin10
  N13: J7.pin6, J8.pin6
  N14: J7.pin9, U1.Q3
  N15: J7.pin10, U2.Q3
  N16: J9.pin6, J10.pin6
  N17: J9.pin9, J9.pin10
  N18: J10.pin9, U1.Q4
  N19: J10.pin10, U2.Q4
  N20: J11.pin6, J12.pin6
  N21: J11.pin9, U1.Q5
  N22: J11.pin10, U2.Q5
  N23: J12.pin9, J12.pin10
  N24: J13.pin6, J14.pin6
  N25: J13.pin9, U1.Q6
  N26: J13.pin10, U2.Q6
  N27: J14.pin9, J14.pin10
  N28: J15.pin6, J19.pin6
  N29: J15.pin9, U1.Q7
  N30: J15.pin10, U2.Q7
  N31: J19.pin9, J19.pin10, J27.pin4
  N32: J20.pin2, J20.pin3, J21.pin3
  N33: J21.pin2, J22.pin2, J29.pin8
  N34: J22.pin3, J23.pin3
  N35: J23.pin1, J29.pin7
  N36: J23.pin4, J29.pin1
  N37: J24.pin2, J25.pin2
  N38: J24.pin3, J25.pin3
  N39: J26.pin2, J27.pin2
  N40: J26.pin3, J27.pin3
  N41: J28.pin7, S2.leg0
  N42: J28.pin8, S2.leg1
  N43: U1.GND, J32.pin2
  N44: U1.SH_CP, J31.pin4
  N45: U1.ST_CP, J31.pin5
  N46: U1.DS, J31.pin6
  N47: U2.MR, J32.pin1
  N48: U2.SH_CP, J31.pin1
  N49: U2.ST_CP, J31.pin2
  N50: U2.DS, J31.pin3
